# Fritzing sketch ManualCtl_NodeMCU (saved by Fritzing 0.8.7b)

parts:
  U1 = LIPO-1000mAh [package=lipo-1000]
  U2 = NodeMCU V3.0
  PART2 = Motor Driver 1A Dual TB6612FNG [part_number=ROB_09457]
  M2 = DC Motor
  M3 = DC Motor
  M4 = DC Motor
  PART1 = Motor Driver 1A Dual TB6612FNG [part_number=ROB_09457]
  M1 = DC Motor

nets:
  N1: U1.+, U2.Vin, PART2.VM, PART1.VM
  GND: U1.-, U2.GND, PART2.GND, PART1.GND
  N2: U2.D0, PART2.BIN2
  N3: U2.D1, PART2.BIN1
  N4: U2.D2, PART2.PWMA, PART2.PWMB, PART1.PWMA, PART1.PWMB
  N5: U2.D3, PART2.AIN1
  N6: U2.D4, PART2.AIN2
  N7: U2.D5, PART1.BIN2
  N8: U2.D6, PART1.BIN1
  N9: U2.D7, PART1.AIN1
  N10: U2.D8, PART1.AIN2
  VCC: U2.3V3, PART2.STBY, PART2.VCC, PART1.STBY, PART1.VCC
  N11: PART2.A01, M4.pin_2
  N12: PART2.A02, M4.pin_1
  N13: PART2.B02, M3.pin_2
  N14: PART2.B01, M3.pin_1
  N15: M2.pin_1, PART1.B01
  N16: M2.pin_2, PART1.B02
  N17: PART1.A01, M1.pin_2
  N18: PART1.A02, M1.pin_1

custom parts:
  NodeMCU V3.0: ESP8266 based NodeMCU
  Motor Driver 1A Dual TB6612FNG: The TB6612FNG motor driver can control up to two DC motors at a constant current of 1.2A (3.2A peak). Two input signals (IN1 and IN2) can be used to control the motor in one of four function modes - CW, CCW, short-brake, and stop. The two motor outputs (A and B) can be separately controlled, the speed of each motor is controlled via a PWM input signal with a frequency up to 100kHz. The STBY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
