# Fritzing sketch NodeMCU_DRV8835 (saved by Fritzing 0.8.7b)

parts:
  U1 = NodeMCU V3.0
  U2 = LIPO-1000mAh [package=lipo-1000]
  Part1 = DRV8835 Dual Motor Driver Carrier
  M2 = DC Motor
  M3 = DC Motor

nets:
  N1: U1.D1, Part1.BIN2/BENABLE, Part1.AOUT1, M2.pin_2
  N2: U1.D2, Part1.BIN1/BPHASE
  N3: U1.D3, Part1.AIN2/AENABLE
  N4: U1.D4, Part1.AIN1/APHASE
  GND: U1.GND, U2.-, Part1.GND
  3V3: U1.3V3, Part1.VCC, Part1.VIN
  N5: U1.Vin, U2.+
  N6: Part1.AOUT2, M2.pin_1
  N7: Part1.BOUT1, M3.pin_2
  N8: Part1.BOUT2, M3.pin_1

custom parts:
  NodeMCU V3.0: ESP8266 based NodeMCU
